# Fritzing sketch Robotic Arm Wiring diagram (saved by Fritzing 0.9.3b)
breadboards: 2

parts:
  VCC6 = Battery  # not connected
  VCC7 = Battery
  VCC8 = Battery
  U3 = SWITCH-SPST-2 [package=r_sw_th]
  J3 = Basic Servo
  U5 = ESP32-38PinWide [part_number=ESP32-38PinWide]
  PWM1 = PCA9685 16x12-bit PWM Breakout
  M6 = RioRand LM2596
  J4 = Basic Servo
  J5 = Basic Servo
  J6 = Basic Servo
  M8 = Dagu DGServo 9g (Top view) [part_number=RS001B]
  M9 = Dagu DGServo 9g (Top view) [part_number=RS001B]

nets:
  N1: VCC7.+, U3.O
  N2: VCC8.-, M6.Pin_2
  N3: U3.P, M6.Pin_1
  GND: J3.gnd, PWM1.no_name_yet#501, PWM1.no_name_yet#1000, PWM1.no_name_yet#1001, PWM1.no_name_yet#1002, PWM1.no_name_yet#1003, PWM1.no_name_yet#1004, PWM1.no_name_yet#1005, M6.Pin_4, J4.gnd, J5.gnd, J6.gnd, M8.gnd, M9.gnd
  VCC: J3.vcc, PWM1.no_name_yet#100, PWM1.no_name_yet#101, PWM1.no_name_yet#102, PWM1.no_name_yet#103, PWM1.no_name_yet#104, PWM1.no_name_yet#105, J4.vcc, J5.vcc, J6.vcc, M8.vcc, M9.vcc
  N4: J3.pulse, PWM1.no_name_yet#0
  N5: U5.GND#13, U5.GND#31, U5.GND#37
  N6: U5.5V#18, PWM1.no_name_yet#505, M6.Pin_3
  N7: U5.GPIO21, PWM1.no_name_yet#504
  N8: U5.GPIO22, PWM1.no_name_yet#503
  N9: PWM1.no_name_yet#1, J4.pulse
  N10: PWM1.no_name_yet#2, J5.pulse
  N11: PWM1.no_name_yet#3, J6.pulse
  N12: PWM1.no_name_yet#4, M8.pulse
  N13: PWM1.no_name_yet#5, M9.pulse

notes:
  Base
  Right Shoulder
  Left Shoulder
  Elbow
  Wrist
  Claw

custom parts:
  ESP32-38PinWide: Generic 38-Pin ESP32 with wide format (only access to one side of pins on a breadboard) based on Stephen Lilley's HiLetgo ESP-WROOM-32 ESP32 ESP-32S Development Board.
